// Logisim project cpu design to stu.circ as structural Verilog: 4 circuits, main circuit ◇单周期MIPS(硬布线)
module \单周期MIPS_硬布线  (
  output RegWrite,
  output MemWrite,
  output [31:0] PC,
  output [31:0] IR,
  output [31:0] RDin,
  output [31:0] MDin
);

  wire and_2_out, and_3_out, Branch, cCLK, CLK, mips_alu_1_equal, not_1_out, not_2_out, RST, undriven,
       undriven_2, undriven_3, undriven_4, undriven_5, undriven_6, undriven_7, undriven_8, undriven_9;
  wire [1:0] mips_alu_1_result;
  wire [3:0] mips8control_1_aluop, mips_alu_1_result_3;
  wire [4:0] multiplexer_2_out;
  wire [7:0] mips_alu_1_result_4, mips_alu_1_result_5;
  wire [9:0] mips_alu_1_result_2;
  wire [15:0] \总周期数 ;
  wire [31:0] adder_1_out, adder_2_out, bit_extender_1_out, mips_regifile_1_r1, mips_regifile_1_r2,
       multiplexer_1_out, multiplexer_3_out, multiplexer_4_out, PC_q, ram_1_data, rom_1_data, shifter_1_out;

  Button \u_总复位  (.out(RST));
  // Probe on Branch
  // Probe on multiplexer_1_out
  Multiplexer #(.select(1), .width(32), .disabled("Z"), .enable("false")) multiplexer_1 (
    .in0(adder_1_out), .in1(adder_2_out), .out(multiplexer_1_out), .sel(Branch));
  Clock #(.highDuration(1), .lowDuration(1)) clock_1 (.out(CLK));
  Register #(.width(32), .trigger("rising"), .Select("low")) u_PC (
    .D(multiplexer_1_out), .Q(PC_q), .clk(cCLK), .clr(RST));  // open: en
  // Probe on adder_1_out
  and and_1 (cCLK, CLK, not_1_out);
  // Probe on PC_q
  Adder #(.width(32)) adder_1 (.a(PC_q), .b(32'h4), .out(adder_1_out));  // open: cin, cout
  // Probe on \总周期数 
  // Probe on \总周期数 
  // Probe on not_1_out
  not not_1 (not_1_out, undriven);
  // Probe on rom_1_data
  ROM #(.addrWidth(10), .dataWidth(32), .Select("low")) rom_1 (.addr(PC_q[11:2]), .data(rom_1_data));
  Adder #(.width(32)) adder_2 (.a(adder_1_out), .b(shifter_1_out), .out(adder_2_out));  // open: cin, cout
  // Probe on rom_1_data[15:0]
  // Probe on rom_1_data[5:0]
  // Probe on rom_1_data[31:26]
  Multiplexer #(.select(1), .width(5), .disabled("Z"), .enable("false")) multiplexer_2 (
    .in0(rom_1_data[20:16]), .in1(rom_1_data[15:11]), .out(multiplexer_2_out), .sel(undriven_2));
  // Probe on multiplexer_2_out
  MIPS8control mips8control_1 (.OP(rom_1_data[31:26]), .F(rom_1_data[5:0]), .AluOp(mips8control_1_aluop));
  MIPS_Regifile mips_regifile_1 (
    .Din(multiplexer_4_out), .Clk(cCLK), .R1(mips_regifile_1_r1), .R2(mips_regifile_1_r2), .WE(undriven_3),
    .W_num(multiplexer_2_out), .R1_num(rom_1_data[25:21]), .R2_num(rom_1_data[20:16]));
  assign bit_extender_1_out = {{16{rom_1_data[15]}}, rom_1_data[15:0]};  // Bit_Extender bit_extender_1
  // Probe on mips_regifile_1_r1
  // Probe on mips_regifile_1_r2
  // Probe on undriven_9
  Multiplexer #(.select(1), .width(32), .disabled("Z"), .enable("false")) multiplexer_3 (
    .in0(mips_regifile_1_r2), .in1(bit_extender_1_out), .out(multiplexer_3_out), .sel(undriven_9));
  // Probe on bit_extender_1_out
  Shifter #(.width(32), .shift("ll")) shifter_1 (.in(bit_extender_1_out), .\dist (5'b00010), .out(shifter_1_out));
  // Probe on mips8control_1_aluop
  MIPS_ALU mips_alu_1 (
    .X(mips_regifile_1_r1), .Y(multiplexer_3_out), .AluOP(mips8control_1_aluop), .Equal(mips_alu_1_equal),
    .Result({mips_alu_1_result_5, mips_alu_1_result_4, mips_alu_1_result_3, mips_alu_1_result_2, mips_alu_1_result}));  // open: Result_2
  and and_2 (and_2_out, mips_alu_1_equal, undriven_4);
  and and_3 (and_3_out, undriven_5, not_2_out);
  not not_2 (not_2_out, mips_alu_1_equal);
  // Probe on {mips_alu_1_result_5, mips_alu_1_result_4, mips_alu_1_result_3, mips_alu_1_result_2, mips_alu_1_result}
  or or_1 (Branch, and_2_out, and_3_out);
  RAM #(.addrWidth(10), .dataWidth(32), .bus("separate"), .Select("high")) ram_1 (
    .addr(mips_alu_1_result_2), .din(mips_regifile_1_r2), .data(ram_1_data), .str(undriven_8), .clk(cCLK),
    .ld(undriven_7), .clr(RST));  // open: sel
  // Probe on ram_1_data
  // Probe on undriven_6
  Multiplexer #(.select(1), .width(32), .disabled("Z"), .enable("false")) multiplexer_4 (
    .in0({mips_alu_1_result_5, mips_alu_1_result_4, mips_alu_1_result_3, mips_alu_1_result_2, mips_alu_1_result}),
    .in1(ram_1_data), .out(multiplexer_4_out), .sel(undriven_6));

  // Notes on the sheet:
  //   程序运行结束后可停机，查看数据存储器中80单元的排序情况是有符号降序
  //   总周期数参考值：224
  //   contents of rom_1 (hex, n*v repeats v):
  //   20120009 2010ffff 20110000 ae300000 22100001 22310004 2252ffff 1640fffb 8020 20110020 8e130000
  //   8e340000 274402a 11000002 ae330000 ae140000 2231fffc 1611fff8 22100004 20110020 1611fff5 2002000a c
  //   SysCall
  //   RegDst
  //   Beq
  //   Bne
  //   AluOp
  //   AluSrc
  //   RegWrite
  //   为方便自动评测，需要输出PC，IR，寄存器文件写入端口RDin，内存写入端口MDin等信号
  //   MemtoReg
  //   MemRead
  //   MemWrite
  //   MemWrite
  //   MemtoReg
endmodule

module MIPS_Regifile (
  input  [31:0] Din,
  input  Clk,
  input  WE,
  input  [4:0] R1_num,
  input  [4:0] R2_num,
  input  [4:0] W_num,
  output [31:0] R1,
  output [31:0] R2
);

  // RegisterFile registerfile_1: pin names not known; wires that end beside it: Din, Clk, WE, W_num, R1_num, R2_num, R1, R2
endmodule

// ALU
module MIPS_ALU (
  input  [31:0] X,
  input  [31:0] Y,
  input  [3:0] AluOP,
  output Equal,
  output [31:0] Result,
  output [31:0] Result_2
);

  wire [0:0] comparator_1_lt, comparator_2_lt;
  wire [31:0] adder_1_out, AND_out, divider_1_out, divider_1_rem, multiplier_1_cout, multiplier_1_out,
       NOR_out, OR_out, shifter_1_out, shifter_2_out, shifter_3_out, subtractor_1_out, XOR_out;

  assign AND_out = X & Y;  // AND_Gate AND, 32 bits wide
  assign OR_out = X | Y;  // OR_Gate OR, 32 bits wide
  Shifter #(.width(32), .shift("ll")) shifter_1 (.in(X), .\dist (Y[4:0]), .out(shifter_1_out));
  Shifter #(.width(32), .shift("ar")) shifter_2 (.in(X), .\dist (Y[4:0]), .out(shifter_2_out));
  Shifter #(.width(32), .shift("lr")) shifter_3 (.in(X), .\dist (Y[4:0]), .out(shifter_3_out));
  Multiplier #(.width(32)) multiplier_1 (.a(X), .b(Y), .out(multiplier_1_out), .cout(multiplier_1_cout));  // open: cin
  Divider #(.width(32)) divider_1 (.a(X), .b(Y), .out(divider_1_out), .rem(divider_1_rem));  // open: upper
  Adder #(.width(32)) adder_1 (.a(X), .b(Y), .out(adder_1_out));  // open: cin, cout
  Subtractor #(.width(32)) subtractor_1 (.a(X), .b(Y), .out(subtractor_1_out));  // open: bin, bout
  assign XOR_out = X ^ Y;  // XOR_Gate XOR, 32 bits wide
  assign NOR_out = ~(X | Y);  // NOR_Gate NOR, 32 bits wide
  Comparator #(.width(32), .mode("twosComplement")) comparator_1 (
    .a(X), .b(Y), .eq(Equal), .lt(comparator_1_lt[0]));  // open: gt
  Comparator #(.width(32), .mode("unsigned")) comparator_2 (.a(X), .b(Y), .lt(comparator_2_lt[0]));  // open: gt, eq
  Multiplexer #(.select(4), .width(32), .disabled("Z"), .enable("false")) multiplexer_1 (
    .in0(shifter_1_out), .in1(shifter_2_out), .in2(shifter_3_out), .in3(multiplier_1_out),
    .in4(divider_1_out), .in5(adder_1_out), .in6(subtractor_1_out), .in7(AND_out), .in8(OR_out),
    .in9(XOR_out), .in10(NOR_out), .in11({{31{1'b0}}, comparator_1_lt[0]}),
    .in12({{31{1'b0}}, comparator_2_lt[0]}), .in13({32{1'b0}}), .in14({32{1'b0}}), .in15({32{1'b0}}),
    .out(Result), .sel(AluOP));
  Multiplexer #(.select(4), .width(32), .disabled("Z"), .enable("false")) multiplexer_2 (
    .in0({32{1'b0}}), .in1({32{1'b0}}), .in2({32{1'b0}}), .in3(multiplier_1_cout), .in4(divider_1_rem),
    .in5({32{1'b0}}), .in6({32{1'b0}}), .in7({32{1'b0}}), .in8({32{1'b0}}), .in9({32{1'b0}}),
    .in10({32{1'b0}}), .in11({32{1'b0}}), .in12({32{1'b0}}), .in13({32{1'b0}}), .in14({32{1'b0}}),
    .in15({32{1'b0}}), .out(Result_2), .sel(AluOP));

  // Other names for the same wires on the sheet: Result2[31:0] = Result_2; S[3:0] = AluOP

  // Notes on the sheet:
  //   不要改变此引脚区域内容，也不要改变ALU封装形式
  //   输入引脚
  //   输出引脚
endmodule

// 8指令单周期控制器
module MIPS8control (
  input  [5:0] OP,
  input  [5:0] F,
  output [3:0] AluOp
);


  // Other names for the same wires on the sheet: S0 = AluOp[0]; S1 = AluOp[1]; S2 = AluOp[2]; S3 = AluOp[3]
endmodule
