// Logisim project Mutil-cycles-CPU-micro(to stu).circ as structural Verilog: 6 circuits, main circuit ◇多周期MIPS(待完善)
module \多周期MIPS_待完善  (
);

  wire AluSave, and_2_out, and_3_out, cCLK, CLK, comparator_1_eq, Jmp, MemRead, MemWrite, mips_alu_1_equal,
       not_1_out, not_2_out, or_1_out, RST, \多周期微程序控制器_待写入微程序_1_beq , \多周期微程序控制器_待写入微程序_1_bne ,
       \多周期微程序控制器_待写入微程序_1_iord , \多周期微程序控制器_待写入微程序_1_irwrite , \多周期微程序控制器_待写入微程序_1_memtoreg ,
       \多周期微程序控制器_待写入微程序_1_pcsrc , \多周期微程序控制器_待写入微程序_1_pcwrite , \多周期微程序控制器_待写入微程序_1_regdst ,
       \多周期微程序控制器_待写入微程序_1_regwrite , \多周期微程序控制器_待写入微程序_1_syscall ;
  wire [1:0] \多周期微程序控制器_待写入微程序_1_alusrca , \多周期微程序控制器_待写入微程序_1_alusrcb ;
  wire [3:0] \多周期微程序控制器_待写入微程序_1_aluop ;
  wire [4:0] multiplexer_2_out, \微地址 ;
  wire [15:0] \总周期数 ;
  wire [31:0] A_q, bit_extender_1_out, C_q, DR_q, IR_q, mips_alu_1_result, mips_probe_1_p1, mips_probe_2_p1,
       mips_probe_6_p1, mips_regifile_1_r1, mips_regifile_1_r2, multiplexer_1_out, multiplexer_3_out,
       multiplexer_4_out, multiplexer_5_out, PC_q, shifter_1_out;

  Button \u_总复位  (.out(RST));
  Register #(.width(32), .trigger("rising"), .Select("low")) PC (
    .D(mips_probe_6_p1), .en(or_1_out), .Q(PC_q), .clk(cCLK), .clr(RST));
  Multiplexer #(.select(1), .width(32), .disabled("Z"), .enable("false")) multiplexer_1 (
    .in0(PC_q), .in1(C_q), .out(multiplexer_1_out), .sel(\多周期微程序控制器_待写入微程序_1_iord ));
  Comparator #(.width(5), .mode("twosComplement")) comparator_1 (
    .a(\微地址 ), .b(5'b01111), .eq(comparator_1_eq));  // open: gt, lt
  Clock #(.highDuration(1), .lowDuration(1)) clock_1 (.out(CLK));
  not not_1 (not_1_out, comparator_1_eq);
  and and_1 (cCLK, CLK, not_2_out);
  not not_2 (not_2_out, \多周期微程序控制器_待写入微程序_1_syscall );
  // Mips_Probe mips_probe_1: pin names not known; wires that end beside it: mips_probe_1_p1
  RAM #(.addrWidth(10), .dataWidth(32), .bus("separate"), .Select("high")) ram_1 (
    .addr(multiplexer_1_out[11:2]), .din(mips_probe_2_p1), .data(mips_probe_1_p1), .str(MemWrite),
    .clk(cCLK), .ld(MemRead));  // open: sel, clr
  Counter #(.width(16), .max('hffff), .ongoal("wrap"), .trigger("rising"), .behavior("old")) counter_1 (
    .count(not_1_out), .Q(\总周期数 ), .clk(cCLK));  // open: load, D, carry, clr, preset
  // Probe on \总周期数 
  // Probe on \微地址 
  Register #(.width(32), .trigger("rising"), .Select("low")) IR (
    .D(mips_probe_1_p1), .en(\多周期微程序控制器_待写入微程序_1_irwrite ), .Q(IR_q), .clk(cCLK));  // open: clr
  Register #(.width(32), .trigger("rising"), .Select("low")) DR (
    .D(mips_probe_1_p1), .Q(DR_q), .clk(cCLK));  // open: en, clr
  Multiplexer #(.select(1), .width(5), .disabled("Z"), .enable("false")) multiplexer_2 (
    .in0(IR_q[20:16]), .in1(IR_q[15:11]), .out(multiplexer_2_out), .sel(\多周期微程序控制器_待写入微程序_1_regdst ));
  \多周期微程序控制器_待写入微程序  \u_多周期微程序控制器_待写入微程序_1  (
    .PcWrite(\多周期微程序控制器_待写入微程序_1_pcwrite ), .Beq(\多周期微程序控制器_待写入微程序_1_beq ),
    .PCsrc(\多周期微程序控制器_待写入微程序_1_pcsrc ), .AluSrcB(\多周期微程序控制器_待写入微程序_1_alusrcb ),
    .AluSrcA(\多周期微程序控制器_待写入微程序_1_alusrca ), .RegWrite(\多周期微程序控制器_待写入微程序_1_regwrite ),
    .MemToReg(\多周期微程序控制器_待写入微程序_1_memtoreg ), .RegDst(\多周期微程序控制器_待写入微程序_1_regdst ),
    .IorD(\多周期微程序控制器_待写入微程序_1_iord ), .MemWrite(MemWrite), .MemRead(MemRead),
    .IrWrite(\多周期微程序控制器_待写入微程序_1_irwrite ), .Bne(\多周期微程序控制器_待写入微程序_1_bne ), .CLK(cCLK), .\当前微指令地址 (\微地址 ),
    .RST(RST), .OP(IR_q[31:26]), .Func(IR_q[5:0]), .Jmp(Jmp), .Syscall(\多周期微程序控制器_待写入微程序_1_syscall ),
    .AluOp(\多周期微程序控制器_待写入微程序_1_aluop ), .AluSave(AluSave));
  Multiplexer #(.select(1), .width(32), .disabled("Z"), .enable("false")) multiplexer_3 (
    .in0(C_q), .in1(DR_q), .out(multiplexer_3_out), .sel(\多周期微程序控制器_待写入微程序_1_memtoreg ));
  // Mips_Probe mips_probe_2: pin names not known; wires that end beside it: mips_probe_2_p1
  // Mips_Probe mips_probe_3: pin names not known; wires that end beside it: PC_q
  MIPS_Regifile mips_regifile_1 (
    .Din(multiplexer_3_out), .Clk(cCLK), .R1(mips_regifile_1_r1), .R2(mips_regifile_1_r2),
    .WE(\多周期微程序控制器_待写入微程序_1_regwrite ), .W_num(multiplexer_2_out), .R1_num(IR_q[25:21]), .R2_num(IR_q[20:16]));
  assign bit_extender_1_out = {{16{IR_q[15]}}, IR_q[15:0]};  // Bit_Extender bit_extender_1
  Register #(.width(32), .trigger("rising"), .Select("low")) A (
    .D(mips_regifile_1_r1), .Q(A_q), .clk(cCLK));  // open: en, clr
  Register #(.width(32), .trigger("rising"), .Select("low")) B (
    .D(mips_regifile_1_r2), .Q(mips_probe_2_p1), .clk(cCLK));  // open: en, clr
  Multiplexer #(.select(2), .width(32), .disabled("Z"), .enable("false")) multiplexer_4 (
    .in0(PC_q), .in1(A_q), .out(multiplexer_4_out), .sel(\多周期微程序控制器_待写入微程序_1_alusrca ));  // open: in2, in3
  // Mips_Probe mips_probe_4: pin names not known; wires that end beside it: mips_probe_2_p1
  Shifter #(.width(32), .shift("ll")) shifter_1 (.in(bit_extender_1_out), .\dist (5'b00010), .out(shifter_1_out));
  Multiplexer #(.select(2), .width(32), .disabled("Z"), .enable("false")) multiplexer_5 (
    .in0(mips_probe_2_p1), .in1(32'h4), .in2(bit_extender_1_out), .in3(shifter_1_out),
    .out(multiplexer_5_out), .sel(\多周期微程序控制器_待写入微程序_1_alusrcb ));
  and and_2 (and_2_out, \多周期微程序控制器_待写入微程序_1_bne , ~mips_alu_1_equal);  // AND_Gate
  MIPS_ALU mips_alu_1 (
    .X(multiplexer_4_out), .Y(multiplexer_5_out), .AluOP(\多周期微程序控制器_待写入微程序_1_aluop ),
    .Equal(mips_alu_1_equal), .Result(mips_alu_1_result));  // open: Result_2
  // Mips_Probe mips_probe_5: pin names not known; wires that end beside it: mips_alu_1_result
  // Mips_Probe mips_probe_6: pin names not known; wires that end beside it: mips_probe_6_p1
  and and_3 (and_3_out, \多周期微程序控制器_待写入微程序_1_beq , mips_alu_1_equal);
  // Mips_Probe mips_probe_7: pin names not known; wires that end beside it: \多周期微程序控制器_待写入微程序_1_aluop , mips_alu_1_result
  Register #(.width(32), .trigger("rising"), .Select("low")) C (
    .D(mips_alu_1_result), .en(AluSave), .Q(C_q), .clk(cCLK));  // open: clr
  or or_1 (or_1_out, \多周期微程序控制器_待写入微程序_1_pcwrite , and_3_out, and_2_out);
  Multiplexer #(.select(1), .width(32), .disabled("Z"), .enable("false")) multiplexer_6 (
    .in0(mips_alu_1_result), .in1(C_q), .out(mips_probe_6_p1), .sel(\多周期微程序控制器_待写入微程序_1_pcsrc ));

  // Notes on the sheet:
  //   PCEnable
  //   IorD
  //   存储器
  //   IrWrite
  //   MemWrite
  //   MemRead
  //   rs
  //   rt
  //   rd
  //   Imm16
  //   总周期数参考值：954
  //   Syscall
  //   IorD
  //   IrWrite
  //   Op
  //   Func
  //   uAddr
  //   RegDst
  //   RegDst
  //   PcWrite
  //   Beq
  //   Bne
  //   PcSrc
  //   AluOp
  //   AluSave
  //   AluSrcB
  //   AluSrcA
  //   RegWrite
  //   MemToReg
  //   MemToReg
  //   RegWrite
  //   AluSrcA
  //   AluSrcB
  //   AluOp
  //   PcEnable
  //   PCSrc
endmodule

// 微程序控制器
module \多周期微程序控制器_待写入微程序  (
  input  [5:0] OP,
  input  [5:0] Func,
  input  CLK,
  input  RST,
  output Jmp,
  output Syscall,
  output Bne,
  output Beq,
  output AluSave,
  output [4:0] \当前微指令地址 ,
  output MemRead,
  output MemWrite,
  output RegWrite,
  output [3:0] AluOp,
  output PcWrite,
  output PCsrc,
  output RegDst,
  output MemToReg,
  output [1:0] AluSrcB,
  output [1:0] AluSrcA,
  output IrWrite,
  output IorD
);

  wire P;
  wire [4:0] multiplexer_1_out, rom_1_data, \微程序地址转移封装电路_1_s0 ;

  \微程序地址转移封装电路  \u_微程序地址转移封装电路_1  (
    .OP(OP), .F(Func), .S4(\微程序地址转移封装电路_1_s0 [4]), .S3(\微程序地址转移封装电路_1_s0 [3]), .S2(\微程序地址转移封装电路_1_s0 [2]),
    .S1(\微程序地址转移封装电路_1_s0 [1]), .S0(\微程序地址转移封装电路_1_s0 [0]));
  // Probe on \微程序地址转移封装电路_1_s0 
  Register #(.width(5), .trigger("rising"), .Select("low")) register_1 (
    .D(multiplexer_1_out), .Q(\当前微指令地址 ), .clk(CLK), .clr(RST));  // open: en
  Multiplexer #(.select(1), .width(5), .disabled("Z"), .enable("false")) multiplexer_1 (
    .in0(rom_1_data), .in1(\微程序地址转移封装电路_1_s0 ), .out(multiplexer_1_out), .sel(P));
  ROM #(.addrWidth(5), .dataWidth(28), .Select("high")) rom_1 (
    .addr(\当前微指令地址 ),
    .data({IorD, IrWrite, AluSrcA, AluSrcB, MemToReg, RegDst, PCsrc, PcWrite, RegWrite, MemWrite, MemRead, Beq, Bne, Syscall, Jmp, AluOp, AluSave, P, rom_1_data}));

  // Notes on the sheet:
  //   下址字段
  //   微程序
  //   入口地址
  //   判断逻辑
  //   根据指令进行微程序地址转移
  //   μAR
  //   控制存储器
  //   contents of rom_1 (hex, n*v repeats v):
  //   4448281 20 18002c3 8008004 220000 18002c6 8010000 10002c8 120000 c002ca 1084000 c002cc 1082000
  //   18002ce 20000 1000 2c00ad1 800 10005d3 120000
  //   微指令
  //   微命令
  //   下址字段
  //   判断逻辑
endmodule

module \微程序地址转移封装电路  (
  input  [5:0] OP,
  input  [5:0] F,
  output S4,
  output S3,
  output S2,
  output S1,
  output S0
);

  _1 u_1_1 (
    .OP5(OP[5]), .OP4(OP[4]), .OP3(OP[3]), .OP2(OP[2]), .OP1(OP[1]), .OP0(OP[0]), .F0(F[0]), .F1(F[1]),
    .F2(F[2]), .F3(F[3]), .F4(F[4]), .F5(F[5]), .S4(S4), .S3(S3), .S2(S2), .S1(S1), .S0(S0));
endmodule

module MIPS_Regifile (
  input  [31:0] Din,
  input  Clk,
  input  WE,
  input  [4:0] R1_num,
  input  [4:0] W_num,
  input  [4:0] R2_num,
  output [31:0] R1,
  output [31:0] R2
);

  // RegisterFile registerfile_1: pin names not known; wires that end beside it: Din, Clk, WE, W_num, R1_num, R2_num, R1, R2
endmodule

// ALU
module MIPS_ALU (
  input  [31:0] X,
  input  [31:0] Y,
  input  [3:0] AluOP,
  output Equal,
  output [31:0] Result,
  output [31:0] Result_2
);

  wire [0:0] comparator_1_lt, comparator_2_lt;
  wire [31:0] adder_1_out, AND_out, divider_1_out, divider_1_rem, multiplier_1_cout, multiplier_1_out,
       NOR_out, OR_out, shifter_1_out, shifter_2_out, shifter_3_out, subtractor_1_out, XOR_out;

  assign AND_out = X & Y;  // AND_Gate AND, 32 bits wide
  assign OR_out = X | Y;  // OR_Gate OR, 32 bits wide
  Shifter #(.width(32), .shift("ll")) shifter_1 (.in(X), .\dist (Y[4:0]), .out(shifter_1_out));
  Shifter #(.width(32), .shift("ar")) shifter_2 (.in(X), .\dist (Y[4:0]), .out(shifter_2_out));
  Shifter #(.width(32), .shift("lr")) shifter_3 (.in(X), .\dist (Y[4:0]), .out(shifter_3_out));
  Multiplier #(.width(32)) multiplier_1 (.a(X), .b(Y), .out(multiplier_1_out), .cout(multiplier_1_cout));  // open: cin
  Divider #(.width(32)) divider_1 (.a(X), .b(Y), .out(divider_1_out), .rem(divider_1_rem));  // open: upper
  Adder #(.width(32)) adder_1 (.a(X), .b(Y), .out(adder_1_out));  // open: cin, cout
  Subtractor #(.width(32)) subtractor_1 (.a(X), .b(Y), .out(subtractor_1_out));  // open: bin, bout
  assign XOR_out = X ^ Y;  // XOR_Gate XOR, 32 bits wide
  assign NOR_out = ~(X | Y);  // NOR_Gate NOR, 32 bits wide
  Comparator #(.width(32), .mode("twosComplement")) comparator_1 (
    .a(X), .b(Y), .eq(Equal), .lt(comparator_1_lt[0]));  // open: gt
  Comparator #(.width(32), .mode("twosComplement")) comparator_2 (
    .a(X), .b(Y), .lt(comparator_2_lt[0]));  // open: gt, eq
  Multiplexer #(.select(4), .width(32), .disabled("Z"), .enable("false")) multiplexer_1 (
    .in0(shifter_1_out), .in1(shifter_2_out), .in2(shifter_3_out), .in3(multiplier_1_out),
    .in4(divider_1_out), .in5(adder_1_out), .in6(subtractor_1_out), .in7(AND_out), .in8(OR_out),
    .in9(XOR_out), .in10(NOR_out), .in11({{31{1'b0}}, comparator_1_lt[0]}),
    .in12({{31{1'b0}}, comparator_2_lt[0]}), .in13({32{1'b0}}), .in14({32{1'b0}}), .in15({32{1'b0}}),
    .out(Result), .sel(AluOP));
  Multiplexer #(.select(4), .width(32), .disabled("Z"), .enable("false")) multiplexer_2 (
    .in0({32{1'b0}}), .in1({32{1'b0}}), .in2({32{1'b0}}), .in3(multiplier_1_cout), .in4(divider_1_rem),
    .in5({32{1'b0}}), .in6({32{1'b0}}), .in7({32{1'b0}}), .in8({32{1'b0}}), .in9({32{1'b0}}),
    .in10({32{1'b0}}), .in11({32{1'b0}}), .in12({32{1'b0}}), .in13({32{1'b0}}), .in14({32{1'b0}}),
    .in15({32{1'b0}}), .out(Result_2), .sel(AluOP));

  // Other names for the same wires on the sheet: Result2[31:0] = Result_2; S[3:0] = AluOP

  // Notes on the sheet:
  //   不要改变此引脚区域内容，也不要改变ALU封装形式
  //   输入引脚
  //   输出引脚
endmodule

module _1 (
  input  OP5,
  input  OP4,
  input  OP3,
  input  OP2,
  input  OP1,
  input  OP0,
  input  F0,
  input  F1,
  input  F2,
  input  F3,
  input  F4,
  input  F5,
  output S4,
  output S3,
  output S2,
  output S1,
  output S0
);

  wire and_1_out, and_2_out, and_3_out, and_4_out, and_5_out, and_6_out, and_7_out, and_8_out, and_9_out,
       and_10_out, and_11_out, and_12_out, and_13_out, and_14_out, and_15_out, and_16_out, and_17_out,
       and_18_out, and_19_out, and_20_out, and_21_out, not_1_out, not_2_out, not_3_out, not_4_out, not_5_out,
       not_6_out, not_7_out, not_8_out, not_9_out, not_10_out, not_11_out, not_12_out, not_13_out,
       not_14_out, not_15_out, not_16_out, not_17_out, not_18_out, not_19_out, not_20_out, not_21_out,
       not_22_out, not_23_out, not_24_out, not_25_out, not_26_out, not_27_out, not_28_out, not_29_out,
       not_30_out, not_31_out, not_32_out, not_33_out, not_34_out, not_35_out, not_36_out, not_37_out,
       not_38_out, not_39_out, not_40_out, not_41_out, not_42_out, not_43_out, not_44_out, not_45_out,
       not_46_out, not_47_out, not_48_out, not_49_out, not_50_out, not_51_out, not_52_out, not_53_out,
       not_54_out, not_55_out, not_56_out, not_57_out, not_58_out, not_59_out, not_60_out, not_61_out,
       not_62_out, not_63_out, not_64_out, not_65_out, not_66_out, not_67_out, not_68_out, not_69_out,
       not_70_out, not_71_out, not_72_out, not_73_out, not_74_out, not_75_out, not_76_out, not_77_out,
       not_78_out, not_79_out, not_80_out, not_81_out, not_82_out, not_83_out, not_84_out, not_85_out,
       not_86_out, not_87_out, not_88_out, not_89_out, not_90_out, not_91_out, not_92_out, not_93_out,
       not_94_out, not_95_out, not_96_out, not_97_out, not_98_out, not_99_out, not_100_out, not_101_out,
       not_102_out, not_103_out, not_104_out, not_105_out, not_106_out, not_107_out, not_108_out,
       not_109_out, not_110_out, not_111_out, not_112_out, not_113_out, not_114_out, not_115_out,
       not_116_out, not_117_out, not_118_out, not_119_out, not_120_out, not_121_out, not_122_out,
       not_123_out, not_124_out, not_125_out, not_126_out, not_127_out, not_128_out, not_129_out,
       not_130_out, not_131_out, not_132_out, not_133_out, not_134_out, not_135_out, not_136_out,
       not_137_out, not_138_out, not_139_out, not_140_out;

  not not_1 (not_1_out, OP5);
  not not_2 (not_2_out, OP4);
  not not_3 (not_3_out, OP3);
  not not_4 (not_4_out, OP2);
  not not_5 (not_5_out, OP1);
  not not_6 (not_6_out, OP0);
  not not_7 (not_7_out, F4);
  not not_8 (not_8_out, F2);
  not not_9 (not_9_out, F0);
  not not_10 (not_10_out, OP5);
  not not_11 (not_11_out, OP4);
  not not_12 (not_12_out, OP3);
  not not_13 (not_13_out, OP2);
  not not_14 (not_14_out, OP0);
  not not_15 (not_15_out, OP5);
  not not_16 (not_16_out, OP4);
  not not_17 (not_17_out, OP3);
  not not_18 (not_18_out, OP2);
  not not_19 (not_19_out, OP1);
  not not_20 (not_20_out, OP0);
  not not_21 (not_21_out, F5);
  not not_22 (not_22_out, F4);
  not not_23 (not_23_out, F1);
  not not_24 (not_24_out, F0);
  not not_25 (not_25_out, OP5);
  not not_26 (not_26_out, OP4);
  not not_27 (not_27_out, OP3);
  not not_28 (not_28_out, OP1);
  not not_29 (not_29_out, OP0);
  not not_30 (not_30_out, OP5);
  not not_31 (not_31_out, OP4);
  not not_32 (not_32_out, OP3);
  not not_33 (not_33_out, OP1);
  not not_34 (not_34_out, OP5);
  not not_35 (not_35_out, OP4);
  not not_36 (not_36_out, OP2);
  not not_37 (not_37_out, OP1);
  not not_38 (not_38_out, OP0);
  not not_39 (not_39_out, OP5);
  not not_40 (not_40_out, OP4);
  not not_41 (not_41_out, OP3);
  not not_42 (not_42_out, OP2);
  not not_43 (not_43_out, OP1);
  not not_44 (not_44_out, OP0);
  not not_45 (not_45_out, F4);
  not not_46 (not_46_out, F3);
  not not_47 (not_47_out, F2);
  not not_48 (not_48_out, F1);
  not not_49 (not_49_out, F0);
  not not_50 (not_50_out, OP5);
  not not_51 (not_51_out, OP4);
  not not_52 (not_52_out, OP3);
  not not_53 (not_53_out, OP2);
  not not_54 (not_54_out, OP1);
  not not_55 (not_55_out, OP0);
  not not_56 (not_56_out, F5);
  not not_57 (not_57_out, F4);
  not not_58 (not_58_out, F1);
  not not_59 (not_59_out, F0);
  not not_60 (not_60_out, OP5);
  not not_61 (not_61_out, OP4);
  not not_62 (not_62_out, OP2);
  not not_63 (not_63_out, OP1);
  not not_64 (not_64_out, OP0);
  not not_65 (not_65_out, OP4);
  not not_66 (not_66_out, OP2);
  not not_67 (not_67_out, OP5);
  not not_68 (not_68_out, OP4);
  not not_69 (not_69_out, OP3);
  not not_70 (not_70_out, OP2);
  not not_71 (not_71_out, OP1);
  not not_72 (not_72_out, OP0);
  not not_73 (not_73_out, F4);
  not not_74 (not_74_out, F3);
  not not_75 (not_75_out, F2);
  not not_76 (not_76_out, F1);
  not not_77 (not_77_out, F0);
  not not_78 (not_78_out, OP5);
  not not_79 (not_79_out, OP4);
  not not_80 (not_80_out, OP3);
  not not_81 (not_81_out, OP2);
  not not_82 (not_82_out, OP1);
  not not_83 (not_83_out, OP0);
  not not_84 (not_84_out, F4);
  not not_85 (not_85_out, F2);
  not not_86 (not_86_out, F0);
  not not_87 (not_87_out, OP5);
  not not_88 (not_88_out, OP4);
  not not_89 (not_89_out, OP3);
  not not_90 (not_90_out, OP2);
  not not_91 (not_91_out, OP1);
  not not_92 (not_92_out, OP0);
  not not_93 (not_93_out, F5);
  not not_94 (not_94_out, F4);
  not not_95 (not_95_out, F1);
  not not_96 (not_96_out, F0);
  not not_97 (not_97_out, OP5);
  not not_98 (not_98_out, OP4);
  not not_99 (not_99_out, OP3);
  not not_100 (not_100_out, OP1);
  not not_101 (not_101_out, OP4);
  not not_102 (not_102_out, OP3);
  not not_103 (not_103_out, OP2);
  not not_104 (not_104_out, OP5);
  not not_105 (not_105_out, OP4);
  not not_106 (not_106_out, OP3);
  not not_107 (not_107_out, OP2);
  not not_108 (not_108_out, OP1);
  not not_109 (not_109_out, OP0);
  not not_110 (not_110_out, F4);
  not not_111 (not_111_out, F3);
  not not_112 (not_112_out, F2);
  not not_113 (not_113_out, F1);
  not not_114 (not_114_out, F0);
  not not_115 (not_115_out, OP5);
  not not_116 (not_116_out, OP4);
  not not_117 (not_117_out, OP3);
  not not_118 (not_118_out, OP2);
  not not_119 (not_119_out, OP1);
  not not_120 (not_120_out, OP0);
  not not_121 (not_121_out, F5);
  not not_122 (not_122_out, F4);
  not not_123 (not_123_out, F1);
  not not_124 (not_124_out, F0);
  not not_125 (not_125_out, OP5);
  not not_126 (not_126_out, OP4);
  not not_127 (not_127_out, OP3);
  not not_128 (not_128_out, OP1);
  not not_129 (not_129_out, OP0);
  not not_130 (not_130_out, OP5);
  not not_131 (not_131_out, OP4);
  not not_132 (not_132_out, OP3);
  not not_133 (not_133_out, OP1);
  not not_134 (not_134_out, OP5);
  not not_135 (not_135_out, OP4);
  not not_136 (not_136_out, OP2);
  not not_137 (not_137_out, OP1);
  not not_138 (not_138_out, OP0);
  not not_139 (not_139_out, OP4);
  not not_140 (not_140_out, OP2);
  and and_1 (and_1_out, not_1_out, not_2_out, not_3_out, not_4_out, not_5_out, not_6_out, F5, not_7_out, F3, not_8_out, F1, not_9_out);
  and and_2 (and_2_out, not_10_out, not_11_out, not_12_out, not_13_out, OP1, not_14_out);
  and and_3 (and_3_out, not_15_out, not_16_out, not_17_out, not_18_out, not_19_out, not_20_out, not_21_out, not_22_out, F3, F2, not_23_out, not_24_out);
  and and_4 (and_4_out, not_25_out, not_26_out, not_27_out, OP2, not_28_out, not_29_out);
  and and_5 (and_5_out, not_30_out, not_31_out, not_32_out, OP2, not_33_out, OP0);
  and and_6 (and_6_out, not_34_out, not_35_out, OP3, not_36_out, not_37_out, not_38_out);
  and and_7 (and_7_out, not_39_out, not_40_out, not_41_out, not_42_out, not_43_out, not_44_out, F5, not_45_out, not_46_out, not_47_out, not_48_out, not_49_out);
  and and_8 (and_8_out, not_50_out, not_51_out, not_52_out, not_53_out, not_54_out, not_55_out, not_56_out, not_57_out, F3, F2, not_58_out, not_59_out);
  and and_9 (and_9_out, not_60_out, not_61_out, OP3, not_62_out, not_63_out, not_64_out);
  and and_10 (and_10_out, OP5, not_65_out, OP3, not_66_out, OP1, OP0);
  and and_11 (and_11_out, not_67_out, not_68_out, not_69_out, not_70_out, not_71_out, not_72_out, F5, not_73_out, not_74_out, not_75_out, not_76_out, not_77_out);
  and and_12 (and_12_out, not_78_out, not_79_out, not_80_out, not_81_out, not_82_out, not_83_out, F5, not_84_out, F3, not_85_out, F1, not_86_out);
  and and_13 (and_13_out, not_87_out, not_88_out, not_89_out, not_90_out, not_91_out, not_92_out, not_93_out, not_94_out, F3, F2, not_95_out, not_96_out);
  and and_14 (and_14_out, not_97_out, not_98_out, not_99_out, OP2, not_100_out, OP0);
  and and_15 (and_15_out, OP5, not_101_out, not_102_out, not_103_out, OP1, OP0);
  and and_16 (and_16_out, not_104_out, not_105_out, not_106_out, not_107_out, not_108_out, not_109_out, F5, not_110_out, not_111_out, not_112_out, not_113_out, not_114_out);
  and and_17 (and_17_out, not_115_out, not_116_out, not_117_out, not_118_out, not_119_out, not_120_out, not_121_out, not_122_out, F3, F2, not_123_out, not_124_out);
  and and_18 (and_18_out, not_125_out, not_126_out, not_127_out, OP2, not_128_out, not_129_out);
  and and_19 (and_19_out, not_130_out, not_131_out, not_132_out, OP2, not_133_out, OP0);
  and and_20 (and_20_out, not_134_out, not_135_out, OP3, not_136_out, not_137_out, not_138_out);
  and and_21 (and_21_out, OP5, not_139_out, OP3, not_140_out, OP1, OP0);
  or or_1 (S4, and_1_out, and_2_out);
  or or_2 (S3, and_3_out, and_4_out, and_5_out, and_6_out);
  or or_3 (S2, and_7_out, and_8_out, and_9_out, and_10_out);
  or or_4 (S1, and_11_out, and_12_out, and_13_out, and_14_out, and_15_out);
  or or_5 (S0, and_16_out, and_17_out, and_18_out, and_19_out, and_20_out, and_21_out);
endmodule
