// Logisim project Mutil-cycles-CPU-hardware(to stu)_已修复S3短接.circ as structural Verilog: 7 circuits, main circuit ◇多周期MIPS(硬布线)
module \多周期MIPS_硬布线  (
);

  wire and_1_out, and_2_out, CLK, comparator_1_eq, MemRead, MemWrite, mips_alu_1_equal, not_1_out, or_1_out,
       RST, \多周期硬布线控制器_1_alusrca , \多周期硬布线控制器_1_beq , \多周期硬布线控制器_1_bne , \多周期硬布线控制器_1_iord ,
       \多周期硬布线控制器_1_irwrite , \多周期硬布线控制器_1_memtoreg , \多周期硬布线控制器_1_pcsrc , \多周期硬布线控制器_1_pcwrite ,
       \多周期硬布线控制器_1_regdst , \多周期硬布线控制器_1_regwrite ;
  wire [1:0] \多周期硬布线控制器_1_alusrcb ;
  wire [3:0] \多周期硬布线控制器_1_alu_op , \现态 ;
  wire [4:0] multiplexer_2_out;
  wire [15:0] \总周期数 ;
  wire [31:0] A_q, B_q, bit_extender_1_out, C_q, DR_q, IR_q, mips_alu_1_result, mips_regifile_1_r1,
       mips_regifile_1_r2, multiplexer_1_out, multiplexer_3_out, multiplexer_4_out, multiplexer_5_out,
       multiplexer_6_out, PC_q, ram_1_data, shifter_1_out;

  Button \u_总复位  (.out(RST));
  Register #(.width(32), .trigger("rising"), .Select("low")) PC (
    .D(multiplexer_6_out), .en(or_1_out), .Q(PC_q), .clk(CLK), .clr(RST));
  Multiplexer #(.select(1), .width(32), .disabled("Z"), .enable("false")) multiplexer_1 (
    .in0(PC_q), .in1(C_q), .out(multiplexer_1_out), .sel(\多周期硬布线控制器_1_iord ));
  Clock #(.highDuration(1), .lowDuration(1)) clock_1 (.out(CLK));
  RAM #(.addrWidth(10), .dataWidth(32), .bus("separate"), .Select("high")) ram_1 (
    .addr(multiplexer_1_out[11:2]), .din(B_q), .data(ram_1_data), .str(MemWrite), .clk(CLK), .ld(MemRead));  // open: sel, clr
  Comparator #(.width(4), .mode("twosComplement")) comparator_1 (
    .a(\现态 ), .b(4'b1101), .eq(comparator_1_eq));  // open: gt, lt
  // Probe on \现态 
  not not_1 (not_1_out, comparator_1_eq);
  Register #(.width(32), .trigger("rising"), .Select("low")) IR (
    .D(ram_1_data), .en(\多周期硬布线控制器_1_irwrite ), .Q(IR_q), .clk(CLK));  // open: clr
  Register #(.width(32), .trigger("rising"), .Select("low")) DR (.D(ram_1_data), .Q(DR_q), .clk(CLK));  // open: en, clr
  Counter #(.width(16), .max('hffff), .ongoal("wrap"), .trigger("rising"), .behavior("old")) counter_1 (
    .count(not_1_out), .Q(\总周期数 ), .clk(CLK));  // open: load, D, carry, clr, preset
  Multiplexer #(.select(1), .width(5), .disabled("Z"), .enable("false")) multiplexer_2 (
    .in0(IR_q[20:16]), .in1(IR_q[15:11]), .out(multiplexer_2_out), .sel(\多周期硬布线控制器_1_regdst ));
  // Probe on \总周期数 
  \多周期硬布线控制器  \u_多周期硬布线控制器_1  (
    .RST(RST), .AluSrcB(\多周期硬布线控制器_1_alusrcb ), .OP(IR_q[31:26]), .CLK(CLK), .\当前状态 (\现态 ),
    .IorD(\多周期硬布线控制器_1_iord ), .PCsrc(\多周期硬布线控制器_1_pcsrc ), .AluSrcA(\多周期硬布线控制器_1_alusrca ),
    .MemToReg(\多周期硬布线控制器_1_memtoreg ), .RegDst(\多周期硬布线控制器_1_regdst ), .IrWrite(\多周期硬布线控制器_1_irwrite ),
    .PcWrite(\多周期硬布线控制器_1_pcwrite ), .RegWrite(\多周期硬布线控制器_1_regwrite ), .MemWrite(MemWrite),
    .MemRead(MemRead), .Beq(\多周期硬布线控制器_1_beq ), .Bne(\多周期硬布线控制器_1_bne ), .Func(IR_q[5:0]),
    .ALU_OP(\多周期硬布线控制器_1_alu_op ));
  Multiplexer #(.select(1), .width(32), .disabled("Z"), .enable("false")) multiplexer_3 (
    .in0(C_q), .in1(DR_q), .out(multiplexer_3_out), .sel(\多周期硬布线控制器_1_memtoreg ));
  MIPS_Regifile mips_regifile_1 (
    .Din(multiplexer_3_out), .Clk(CLK), .R1(mips_regifile_1_r1), .R2(mips_regifile_1_r2),
    .WE(\多周期硬布线控制器_1_regwrite ), .W_num(multiplexer_2_out), .R1_num(IR_q[25:21]), .R2_num(IR_q[20:16]));
  assign bit_extender_1_out = {{16{IR_q[15]}}, IR_q[15:0]};  // Bit_Extender bit_extender_1
  Register #(.width(32), .trigger("rising"), .Select("low")) A (
    .D(mips_regifile_1_r1), .Q(A_q), .clk(CLK));  // open: en, clr
  Register #(.width(32), .trigger("rising"), .Select("low")) B (
    .D(mips_regifile_1_r2), .Q(B_q), .clk(CLK));  // open: en, clr
  Multiplexer #(.select(1), .width(32), .disabled("Z"), .enable("false")) multiplexer_4 (
    .in0(PC_q), .in1(A_q), .out(multiplexer_4_out), .sel(\多周期硬布线控制器_1_alusrca ));
  Shifter #(.width(32), .shift("ll")) shifter_1 (.in(bit_extender_1_out), .\dist (5'b00010), .out(shifter_1_out));
  Multiplexer #(.select(2), .width(32), .disabled("Z"), .enable("false")) multiplexer_5 (
    .in0(B_q), .in1(32'h4), .in2(bit_extender_1_out), .in3(shifter_1_out), .out(multiplexer_5_out),
    .sel(\多周期硬布线控制器_1_alusrcb ));
  and and_1 (and_1_out, \多周期硬布线控制器_1_bne , ~mips_alu_1_equal);  // AND_Gate
  MIPS_ALU mips_alu_1 (
    .X(multiplexer_4_out), .Y(multiplexer_5_out), .AluOP(\多周期硬布线控制器_1_alu_op ), .Equal(mips_alu_1_equal),
    .Result(mips_alu_1_result));  // open: Result_2
  and and_2 (and_2_out, \多周期硬布线控制器_1_beq , mips_alu_1_equal);
  Register #(.width(32), .trigger("rising"), .Select("low")) C (
    .D(mips_alu_1_result), .Q(C_q), .clk(CLK));  // open: en, clr
  or or_1 (or_1_out, \多周期硬布线控制器_1_pcwrite , and_2_out, and_1_out);
  Multiplexer #(.select(1), .width(32), .disabled("Z"), .enable("false")) multiplexer_6 (
    .in0(mips_alu_1_result), .in1(C_q), .out(multiplexer_6_out), .sel(\多周期硬布线控制器_1_pcsrc ));

  // Notes on the sheet:
  //   IorD
  //   存储器
  //   Ctrl+K  Command+K触发时钟连续仿真，程序运行结束后可停机，查看数据存储器中80单元的排序情况是有符号降序
  //   完成微程序模式的多周期CPU后，将主机架构图复制到本电路中，替换控制器为硬布线控制器
  //   IRWrite
  //   MemWrite
  //   MemRead
  //   指令字
  //   rs
  //   rt
  //   rd
  //   Imm16
  //   IorD
  //   IRWrite
  //   OP
  //   Func
  //   RegDst
  //   总周期数参考值：891
  //   PcWrite
  //   Beq
  //   Bne
  //   PcSrc
  //   AluOP
  //   AluSrcB
  //   AluSrcA
  //   RegWrite
  //   MemToReg
  //   PcEnable
endmodule

// 硬布线控制器
module \多周期硬布线控制器  (
  input  [5:0] OP,
  input  [5:0] Func,
  input  CLK,
  input  RST,
  output [3:0] ALU_OP,
  output Bne,
  output Beq,
  output MemRead,
  output MemWrite,
  output RegWrite,
  output PcWrite,
  output IrWrite,
  output RegDst,
  output MemToReg,
  output [3:0] \当前状态 ,
  output [1:0] AluSrcB,
  output AluSrcA,
  output PCsrc,
  output IorD
);

  wire comparator_1_eq;
  wire [1:0] ALU_Control;
  wire [3:0] multiplexer_1_out, \状态机fsm_1_n0 ;

  \状态机FSM  \u_状态机fsm_1  (
    .S3(\当前状态 [3]), .N3(\状态机fsm_1_n0 [3]), .S2(\当前状态 [2]), .N2(\状态机fsm_1_n0 [2]), .S1(\当前状态 [1]),
    .N1(\状态机fsm_1_n0 [1]), .S0(\当前状态 [0]), .N0(\状态机fsm_1_n0 [0]), .op(OP), .func(Func));
  Register #(.width(4), .trigger("rising"), .Select("low")) register_1 (
    .D(\状态机fsm_1_n0 ), .en(1'b1), .Q(\当前状态 ), .clk(CLK), .clr(RST), .cs(1'b0), .preset(1'b0));
  \硬布线CU  \u_硬布线cu_1  (
    .S3(\当前状态 [3]), .S2(\当前状态 [2]), .S1(\当前状态 [1]), .S0(\当前状态 [0]), .IorD(IorD), .PcSrc(PCsrc),
    .AluSrcA(AluSrcA), .AluSrcB1(AluSrcB[1]), .AluSrcB0(AluSrcB[0]), .MemToReg(MemToReg), .RegDst(RegDst),
    .IrWrite(IrWrite), .PcWrite(PcWrite), .RegWrite(RegWrite), .MemWrite(MemWrite), .MemRead(MemRead),
    .Beq(Beq), .Bne(Bne), .AluCtrl1(ALU_Control[1]), .AluCtrl0(ALU_Control[0]));
  Multiplexer #(.select(1), .width(4), .disabled("Z"), .enable("false")) multiplexer_1 (
    .in0(4'b0101), .in1(4'b1100), .out(multiplexer_1_out), .sel(comparator_1_eq));
  Comparator #(.width(6), .mode("twosComplement")) comparator_1 (
    .a(Func), .b(6'b101010), .eq(comparator_1_eq));  // open: gt, lt
  Multiplexer #(.select(2), .width(4), .disabled("Z"), .enable("false")) multiplexer_2 (
    .in0(4'b0101), .in1(4'b0101), .in2(multiplexer_1_out), .in3(4'b0101), .out(ALU_OP), .sel(ALU_Control));

  // Notes on the sheet:
  //   指令译码信号
  //   现态
  //   组合逻辑
  //   次态
  //   状态寄存器
  //   硬布线CU（4输入/16输出）
  //   加法
  //   比较
  //   比较
  //   ALU控制器逻辑
  //   根据ALU_Control的值决定运算器运算选择控制信号ALU_OP的值
  //   ALU_Control= 10： 运算方式由Func决定 
  //   ALU_Control= 00 01 11：运算器做加法
endmodule

// 控制器状态机
module \状态机FSM  (
  input  S3,
  input  S2,
  input  S1,
  input  S0,
  input  [5:0] op,
  input  [5:0] func,
  output N3,
  output N2,
  output N1,
  output N0
);

  wire and_1_out, and_2_out, and_3_out, and_4_out, and_5_out, and_6_out, and_7_out, and_8_out, and_9_out,
       and_10_out, and_11_out, and_12_out, and_13_out, and_14_out, and_15_out, and_16_out, and_17_out,
       and_18_out, and_19_out, and_20_out, and_21_out, and_22_out, and_23_out, and_24_out, and_25_out,
       and_26_out, and_27_out, and_28_out, and_29_out, and_30_out, and_31_out, and_32_out, and_33_out,
       and_34_out, and_35_out, and_36_out, and_37_out, and_38_out, and_39_out, and_40_out, and_41_out,
       not_1_out, not_2_out, not_3_out, not_4_out, not_5_out, not_6_out, not_7_out, not_8_out, not_9_out,
       not_10_out, not_11_out, not_12_out, not_13_out, not_14_out, not_15_out, not_16_out, not_17_out,
       not_18_out, not_19_out, not_20_out, not_21_out, not_22_out, not_23_out, not_24_out, not_25_out,
       not_26_out, not_27_out, not_28_out, not_29_out, not_30_out, not_31_out, not_32_out, or_1_out,
       or_2_out, or_3_out, or_4_out, or_5_out, \指令译码逻辑_1_out_3 , \指令译码逻辑_1_out_4 , \指令译码逻辑_1_out_5 ,
       \指令译码逻辑_1_out_6 , \指令译码逻辑_1_out_7 , \指令译码逻辑_1_out_8 , \指令译码逻辑_1_out_9 ;

  \指令译码逻辑  \u_指令译码逻辑_1  (
    .OP(op), .Func(func), .out_3(\指令译码逻辑_1_out_3 ), .out_4(\指令译码逻辑_1_out_4 ), .out_5(\指令译码逻辑_1_out_5 ),
    .out_6(\指令译码逻辑_1_out_6 ), .out_7(\指令译码逻辑_1_out_7 ), .out_8(\指令译码逻辑_1_out_8 ), .out_9(\指令译码逻辑_1_out_9 ));
  Pull_Resistor #(.pull(0)) pull_resistor_1 (.node(S3));
  Pull_Resistor #(.pull(0)) pull_resistor_2 (.node(S2));
  Pull_Resistor #(.pull(0)) pull_resistor_3 (.node(S1));
  Pull_Resistor #(.pull(0)) pull_resistor_4 (.node(S0));
  Pull_Resistor #(.pull(0)) pull_resistor_5 (.node(\指令译码逻辑_1_out_3 ));
  Pull_Resistor #(.pull(0)) pull_resistor_6 (.node(\指令译码逻辑_1_out_4 ));
  Pull_Resistor #(.pull(0)) pull_resistor_7 (.node(\指令译码逻辑_1_out_5 ));
  Pull_Resistor #(.pull(0)) pull_resistor_8 (.node(\指令译码逻辑_1_out_6 ));
  Pull_Resistor #(.pull(0)) pull_resistor_9 (.node(\指令译码逻辑_1_out_7 ));
  Pull_Resistor #(.pull(0)) pull_resistor_10 (.node(\指令译码逻辑_1_out_8 ));
  Pull_Resistor #(.pull(0)) pull_resistor_11 (.node(\指令译码逻辑_1_out_9 ));
  not not_1 (not_1_out, S3);
  not not_2 (not_2_out, S2);
  not not_3 (not_3_out, S1);
  not not_4 (not_4_out, \指令译码逻辑_1_out_3 );
  not not_5 (not_5_out, \指令译码逻辑_1_out_5 );
  not not_6 (not_6_out, S3);
  not not_7 (not_7_out, S2);
  not not_8 (not_8_out, \指令译码逻辑_1_out_4 );
  not not_9 (not_9_out, \指令译码逻辑_1_out_5 );
  not not_10 (not_10_out, \指令译码逻辑_1_out_7 );
  not not_11 (not_11_out, S3);
  not not_12 (not_12_out, S1);
  not not_13 (not_13_out, \指令译码逻辑_1_out_6 );
  not not_14 (not_14_out, \指令译码逻辑_1_out_7 );
  not not_15 (not_15_out, S3);
  not not_16 (not_16_out, S2);
  and and_1 (and_1_out, not_1_out, not_2_out);
  and and_2 (and_2_out, not_3_out, S0);
  and and_3 (and_3_out, not_4_out, not_5_out);
  not not_17 (not_17_out, \指令译码逻辑_1_out_6 );
  and and_4 (and_4_out, not_6_out, not_7_out);
  and and_5 (and_5_out, S0, not_8_out);
  and and_6 (and_6_out, not_9_out, not_10_out);
  not not_18 (not_18_out, \指令译码逻辑_1_out_8 );
  not not_19 (not_19_out, S2);
  and and_7 (and_7_out, not_11_out, not_12_out);
  and and_8 (and_8_out, not_13_out, not_14_out);
  not not_20 (not_20_out, \指令译码逻辑_1_out_9 );
  not not_21 (not_21_out, S3);
  not not_22 (not_22_out, S2);
  not not_23 (not_23_out, S0);
  and and_9 (and_9_out, not_15_out, not_16_out);
  not not_24 (not_24_out, S1);
  not not_25 (not_25_out, \指令译码逻辑_1_out_5 );
  not not_26 (not_26_out, \指令译码逻辑_1_out_8 );
  not not_27 (not_27_out, S3);
  not not_28 (not_28_out, S2);
  and and_10 (and_10_out, and_1_out, and_2_out);
  and and_11 (and_11_out, and_3_out, not_17_out);
  and and_12 (and_12_out, S2, S1);
  and and_13 (and_13_out, S3, S1);
  and and_14 (and_14_out, S3, S2);
  and and_15 (and_15_out, and_4_out, and_5_out);
  and and_16 (and_16_out, and_6_out, not_18_out);
  and and_17 (and_17_out, not_19_out, S1);
  not not_29 (not_29_out, S1);
  and and_18 (and_18_out, and_7_out, S0);
  and and_19 (and_19_out, and_8_out, not_20_out);
  and and_20 (and_20_out, not_21_out, not_22_out);
  and and_21 (and_21_out, S1, not_23_out);
  not not_30 (not_30_out, S3);
  not not_31 (not_31_out, S1);
  and and_22 (and_22_out, and_9_out, not_24_out);
  and and_23 (and_23_out, not_25_out, not_26_out);
  and and_24 (and_24_out, not_27_out, not_28_out);
  not not_32 (not_32_out, S0);
  and and_25 (and_25_out, and_10_out, and_11_out);
  and and_26 (and_26_out, and_12_out, S0);
  and and_27 (and_27_out, and_13_out, S0);
  and and_28 (and_28_out, and_14_out, S0);
  and and_29 (and_29_out, and_15_out, and_16_out);
  and and_30 (and_30_out, and_17_out, S0);
  and and_31 (and_31_out, S2, not_29_out);
  and and_32 (and_32_out, and_18_out, and_19_out);
  and and_33 (and_33_out, and_20_out, and_21_out);
  and and_34 (and_34_out, not_30_out, S2);
  and and_35 (and_35_out, not_31_out, S0);
  and and_36 (and_36_out, and_22_out, and_23_out);
  and and_37 (and_37_out, and_24_out, not_32_out);
  and and_38 (and_38_out, S3, S2);
  or or_1 (or_1_out, and_25_out, and_26_out);
  or or_2 (or_2_out, and_27_out, and_28_out);
  or or_3 (or_3_out, and_29_out, and_30_out);
  and and_39 (and_39_out, and_31_out, S0);
  or or_4 (or_4_out, and_32_out, and_33_out);
  and and_40 (and_40_out, and_34_out, and_35_out);
  or or_5 (or_5_out, and_36_out, and_37_out);
  and and_41 (and_41_out, and_38_out, S0);
  or or_6 (N3, or_1_out, or_2_out);
  or or_7 (N2, or_3_out, and_39_out);
  or or_8 (N1, or_4_out, and_40_out);
  or or_9 (N0, or_5_out, and_41_out);
endmodule

module MIPS_Regifile (
  input  [31:0] Din,
  input  Clk,
  input  WE,
  input  [4:0] R1_num,
  input  [4:0] W_num,
  input  [4:0] R2_num,
  output [31:0] R1,
  output [31:0] R2
);

  // RegisterFile registerfile_1: pin names not known; wires that end beside it: Din, Clk, WE, W_num, R1_num, R2_num, R1, R2
endmodule

// ALU
module MIPS_ALU (
  input  [31:0] X,
  input  [31:0] Y,
  input  [3:0] AluOP,
  output Equal,
  output [31:0] Result,
  output [31:0] Result_2
);

  wire [0:0] comparator_1_lt, comparator_2_lt;
  wire [31:0] adder_1_out, AND_out, divider_1_out, divider_1_rem, multiplier_1_cout, multiplier_1_out,
       NOR_out, OR_out, shifter_1_out, shifter_2_out, shifter_3_out, subtractor_1_out, XOR_out;

  assign AND_out = X & Y;  // AND_Gate AND, 32 bits wide
  assign OR_out = X | Y;  // OR_Gate OR, 32 bits wide
  Shifter #(.width(32), .shift("ll")) shifter_1 (.in(X), .\dist (Y[4:0]), .out(shifter_1_out));
  Shifter #(.width(32), .shift("ar")) shifter_2 (.in(X), .\dist (Y[4:0]), .out(shifter_2_out));
  Shifter #(.width(32), .shift("lr")) shifter_3 (.in(X), .\dist (Y[4:0]), .out(shifter_3_out));
  Multiplier #(.width(32)) multiplier_1 (.a(X), .b(Y), .out(multiplier_1_out), .cout(multiplier_1_cout));  // open: cin
  Divider #(.width(32)) divider_1 (.a(X), .b(Y), .out(divider_1_out), .rem(divider_1_rem));  // open: upper
  Adder #(.width(32)) adder_1 (.a(X), .b(Y), .out(adder_1_out));  // open: cin, cout
  Subtractor #(.width(32)) subtractor_1 (.a(X), .b(Y), .out(subtractor_1_out));  // open: bin, bout
  assign XOR_out = X ^ Y;  // XOR_Gate XOR, 32 bits wide
  assign NOR_out = ~(X | Y);  // NOR_Gate NOR, 32 bits wide
  Comparator #(.width(32), .mode("twosComplement")) comparator_1 (
    .a(X), .b(Y), .eq(Equal), .lt(comparator_1_lt[0]));  // open: gt
  Comparator #(.width(32), .mode("twosComplement")) comparator_2 (
    .a(X), .b(Y), .lt(comparator_2_lt[0]));  // open: gt, eq
  Multiplexer #(.select(4), .width(32), .disabled("Z"), .enable("false")) multiplexer_1 (
    .in0(shifter_1_out), .in1(shifter_2_out), .in2(shifter_3_out), .in3(multiplier_1_out),
    .in4(divider_1_out), .in5(adder_1_out), .in6(subtractor_1_out), .in7(AND_out), .in8(OR_out),
    .in9(XOR_out), .in10(NOR_out), .in11({{31{1'b0}}, comparator_1_lt[0]}),
    .in12({{31{1'b0}}, comparator_2_lt[0]}), .in13({32{1'b0}}), .in14({32{1'b0}}), .in15({32{1'b0}}),
    .out(Result), .sel(AluOP));
  Multiplexer #(.select(4), .width(32), .disabled("Z"), .enable("false")) multiplexer_2 (
    .in0({32{1'b0}}), .in1({32{1'b0}}), .in2({32{1'b0}}), .in3(multiplier_1_cout), .in4(divider_1_rem),
    .in5({32{1'b0}}), .in6({32{1'b0}}), .in7({32{1'b0}}), .in8({32{1'b0}}), .in9({32{1'b0}}),
    .in10({32{1'b0}}), .in11({32{1'b0}}), .in12({32{1'b0}}), .in13({32{1'b0}}), .in14({32{1'b0}}),
    .in15({32{1'b0}}), .out(Result_2), .sel(AluOP));

  // Other names for the same wires on the sheet: Result2[31:0] = Result_2; S[3:0] = AluOP

  // Notes on the sheet:
  //   不要改变此引脚区域内容，也不要改变ALU封装形式
  //   输入引脚
  //   输出引脚
endmodule

module \硬布线CU  (
  input  S3,
  input  S2,
  input  S1,
  input  S0,
  output IorD,
  output PcSrc,
  output AluSrcA,
  output AluSrcB1,
  output AluSrcB0,
  output MemToReg,
  output RegDst,
  output IrWrite,
  output PcWrite,
  output RegWrite,
  output MemWrite,
  output MemRead,
  output Beq,
  output Bne,
  output AluCtrl1,
  output AluCtrl0
);

  wire and_1_out, and_2_out, and_3_out, and_4_out, and_5_out, and_6_out, and_7_out, and_8_out, and_9_out,
       and_10_out, and_11_out, and_12_out, and_13_out, and_14_out, and_15_out, and_16_out, and_17_out,
       and_18_out, and_19_out, and_20_out, and_21_out, and_22_out, and_23_out, and_24_out, and_25_out,
       and_26_out, and_27_out, and_28_out, and_29_out, and_30_out, and_31_out, and_32_out, and_33_out,
       and_34_out, and_35_out, and_36_out, and_37_out, and_38_out, and_39_out, and_40_out, and_41_out,
       and_47_out, and_48_out, and_50_out, and_51_out, and_55_out, and_56_out, not_1_out, not_2_out,
       not_3_out, not_4_out, not_5_out, not_6_out, not_7_out, not_8_out, not_9_out, not_10_out, not_11_out,
       not_12_out, not_13_out, not_14_out, not_15_out, not_16_out, not_17_out, not_18_out, not_19_out,
       not_20_out, not_21_out, not_22_out, not_23_out, not_24_out, not_25_out, not_26_out, not_27_out,
       not_28_out, not_29_out, not_30_out, not_31_out, not_32_out, not_33_out, not_34_out, not_35_out,
       not_36_out, not_37_out, not_38_out, not_39_out, not_40_out, not_41_out, not_42_out, not_43_out,
       not_44_out, not_45_out, not_46_out, or_3_out, or_4_out;

  Pull_Resistor #(.pull(0)) pull_resistor_1 (.node(S3));
  Pull_Resistor #(.pull(0)) pull_resistor_2 (.node(S2));
  Pull_Resistor #(.pull(0)) pull_resistor_3 (.node(S1));
  Pull_Resistor #(.pull(0)) pull_resistor_4 (.node(S0));
  not not_1 (not_1_out, S3);
  and and_1 (and_1_out, not_1_out, not_2_out);
  not not_2 (not_2_out, S2);
  and and_2 (and_2_out, S1, S0);
  and and_3 (and_3_out, S2, S1);
  not not_3 (not_3_out, S0);
  and and_4 (and_4_out, S3, not_4_out);
  not not_4 (not_4_out, S2);
  not not_5 (not_5_out, S1);
  and and_5 (and_5_out, not_5_out, S0);
  and and_6 (and_6_out, S3, S1);
  not not_6 (not_6_out, S0);
  not not_7 (not_7_out, S2);
  and and_7 (and_7_out, not_7_out, S1);
  not not_8 (not_8_out, S0);
  not not_9 (not_9_out, S3);
  and and_8 (and_8_out, not_9_out, S2);
  not not_10 (not_10_out, S2);
  not not_11 (not_11_out, S3);
  and and_9 (and_9_out, not_11_out, not_12_out);
  not not_12 (not_12_out, S1);
  not not_13 (not_13_out, S3);
  and and_10 (and_10_out, not_13_out, not_14_out);
  not not_14 (not_14_out, S2);
  and and_11 (and_11_out, S1, not_15_out);
  not not_15 (not_15_out, S0);
  not not_16 (not_16_out, S3);
  and and_12 (and_12_out, not_16_out, not_17_out);
  not not_17 (not_17_out, S2);
  not not_18 (not_18_out, S1);
  not not_19 (not_19_out, S3);
  and and_13 (and_13_out, not_19_out, S2);
  not not_20 (not_20_out, S1);
  and and_14 (and_14_out, not_20_out, not_21_out);
  not not_21 (not_21_out, S0);
  and and_15 (and_15_out, S3, not_22_out);
  not not_22 (not_22_out, S2);
  not not_23 (not_23_out, S1);
  and and_16 (and_16_out, not_23_out, not_24_out);
  not not_24 (not_24_out, S0);
  not not_25 (not_25_out, S3);
  and and_17 (and_17_out, not_25_out, not_26_out);
  not not_26 (not_26_out, S2);
  not not_27 (not_27_out, S1);
  and and_18 (and_18_out, not_27_out, not_28_out);
  not not_28 (not_28_out, S0);
  not not_29 (not_29_out, S3);
  and and_19 (and_19_out, not_29_out, not_30_out);
  not not_30 (not_30_out, S2);
  not not_31 (not_31_out, S1);
  and and_20 (and_20_out, not_31_out, not_32_out);
  not not_32 (not_32_out, S0);
  and and_21 (and_21_out, S2, not_33_out);
  not not_33 (not_33_out, S1);
  not not_34 (not_34_out, S0);
  and and_22 (and_22_out, S3, not_35_out);
  not not_35 (not_35_out, S1);
  not not_36 (not_36_out, S0);
  and and_23 (and_23_out, S2, S1);
  not not_37 (not_37_out, S0);
  not not_38 (not_38_out, S3);
  and and_24 (and_24_out, not_38_out, not_39_out);
  not not_39 (not_39_out, S2);
  not not_40 (not_40_out, S1);
  and and_25 (and_25_out, not_40_out, not_41_out);
  not not_41 (not_41_out, S0);
  not not_42 (not_42_out, S3);
  and and_26 (and_26_out, not_42_out, not_43_out);
  not not_43 (not_43_out, S2);
  and and_27 (and_27_out, S1, S0);
  and and_28 (and_28_out, S3, not_44_out);
  not not_44 (not_44_out, S2);
  not not_45 (not_45_out, S1);
  and and_29 (and_29_out, not_45_out, S0);
  and and_30 (and_30_out, S3, S1);
  not not_46 (not_46_out, S0);
  and and_31 (and_31_out, S2, S1);
  and and_32 (and_32_out, and_1_out, and_2_out);
  and and_33 (and_33_out, and_3_out, not_3_out);
  and and_34 (and_34_out, and_4_out, and_5_out);
  and and_35 (and_35_out, and_6_out, not_6_out);
  and and_36 (and_36_out, and_7_out, not_8_out);
  and and_37 (and_37_out, and_8_out, S0);
  and and_38 (and_38_out, S3, not_10_out);
  and and_39 (and_39_out, and_9_out, S0);
  and and_40 (and_40_out, and_10_out, and_11_out);
  and and_41 (and_41_out, S3, S1);
  and and_42 (AluSrcB0, and_12_out, not_18_out);
  and and_43 (MemToReg, and_13_out, and_14_out);
  and and_44 (RegDst, and_15_out, and_16_out);
  and and_45 (IrWrite, and_17_out, and_18_out);
  and and_46 (PcWrite, and_19_out, and_20_out);
  and and_47 (and_47_out, and_21_out, not_34_out);
  and and_48 (and_48_out, and_22_out, not_36_out);
  and and_49 (MemWrite, and_23_out, not_37_out);
  and and_50 (and_50_out, and_24_out, and_25_out);
  and and_51 (and_51_out, and_26_out, and_27_out);
  and and_52 (Beq, and_28_out, and_29_out);
  and and_53 (Bne, and_30_out, not_46_out);
  and and_54 (AluCtrl1, and_31_out, S0);
  or or_1 (IorD, and_32_out, and_33_out);
  or or_2 (PcSrc, and_34_out, and_35_out);
  or or_3 (or_3_out, and_36_out, and_37_out);
  and and_55 (and_55_out, and_38_out, S0);
  or or_4 (or_4_out, and_39_out, and_40_out);
  and and_56 (and_56_out, and_41_out, S0);
  or or_5 (RegWrite, and_47_out, and_48_out);
  or or_6 (MemRead, and_50_out, and_51_out);
  or or_7 (AluSrcA, or_3_out, and_55_out);
  or or_8 (AluSrcB1, or_4_out, and_56_out);

  assign AluCtrl0 = 1'b0;
endmodule

module \指令译码逻辑  (
  input  [5:0] OP,
  input  [5:0] Func,
  output out_3,
  output out_4,
  output out_5,
  output out_6,
  output out_7,
  output out_8,
  output out_9
);

  wire and_1_out, and_2_out, not_1_out, not_2_out, not_3_out, not_4_out, not_5_out, not_6_out, not_7_out,
       not_8_out, not_9_out, not_10_out, not_11_out, not_12_out, not_13_out, not_14_out, not_15_out,
       not_16_out, not_17_out, not_18_out, not_19_out, not_20_out, not_21_out, not_22_out, not_23_out,
       not_24_out, not_25_out, not_26_out, not_27_out, not_28_out, not_29_out, not_30_out, not_31_out,
       not_32_out, not_33_out, not_34_out, not_35_out, not_36_out, not_37_out, not_38_out, not_39_out,
       not_40_out, not_41_out, not_42_out, not_43_out, or_1_out;

  Pull_Resistor #(.pull(0)) pull_resistor_1 (.node(Func));
  Pull_Resistor #(.pull(0)) pull_resistor_2 (.node(OP));
  not not_1 (not_1_out, Func[4]);
  not not_2 (not_2_out, Func[3]);
  not not_3 (not_3_out, Func[2]);
  not not_4 (not_4_out, Func[1]);
  not not_5 (not_5_out, Func[0]);
  not not_6 (not_6_out, Func[4]);
  not not_7 (not_7_out, Func[2]);
  not not_8 (not_8_out, Func[0]);
  not not_9 (not_9_out, OP[5]);
  not not_10 (not_10_out, OP[4]);
  not not_11 (not_11_out, OP[2]);
  not not_12 (not_12_out, OP[1]);
  not not_13 (not_13_out, OP[0]);
  not not_14 (not_14_out, OP[4]);
  not not_15 (not_15_out, OP[3]);
  not not_16 (not_16_out, OP[2]);
  not not_17 (not_17_out, OP[4]);
  not not_18 (not_18_out, OP[2]);
  not not_19 (not_19_out, OP[5]);
  not not_20 (not_20_out, OP[4]);
  not not_21 (not_21_out, OP[3]);
  not not_22 (not_22_out, OP[1]);
  not not_23 (not_23_out, OP[0]);
  not not_24 (not_24_out, OP[5]);
  not not_25 (not_25_out, OP[4]);
  not not_26 (not_26_out, OP[3]);
  not not_27 (not_27_out, OP[1]);
  not not_28 (not_28_out, OP[5]);
  not not_29 (not_29_out, OP[4]);
  not not_30 (not_30_out, OP[3]);
  not not_31 (not_31_out, OP[2]);
  not not_32 (not_32_out, OP[1]);
  not not_33 (not_33_out, OP[0]);
  not not_34 (not_34_out, Func[5]);
  not not_35 (not_35_out, Func[4]);
  not not_36 (not_36_out, Func[1]);
  not not_37 (not_37_out, Func[0]);
  and and_1 (and_1_out, Func[5], not_1_out, not_2_out, not_3_out, not_4_out, not_5_out);
  and and_2 (and_2_out, Func[5], not_6_out, Func[3], not_7_out, Func[1], not_8_out);
  and and_3 (out_4, not_9_out, not_10_out, OP[3], not_11_out, not_12_out, not_13_out);
  and and_4 (out_5, OP[5], not_14_out, not_15_out, not_16_out, OP[1], OP[0]);
  and and_5 (out_6, OP[5], not_17_out, OP[3], not_18_out, OP[1], OP[0]);
  and and_6 (out_7, not_19_out, not_20_out, not_21_out, OP[2], not_22_out, not_23_out);
  and and_7 (out_8, not_24_out, not_25_out, not_26_out, OP[2], not_27_out, OP[0]);
  and and_8 (out_9, not_28_out, not_29_out, not_30_out, not_31_out, not_32_out, not_33_out, not_34_out, not_35_out, Func[3], Func[2], not_36_out, not_37_out);
  not not_38 (not_38_out, OP[5]);
  not not_39 (not_39_out, OP[4]);
  not not_40 (not_40_out, OP[3]);
  not not_41 (not_41_out, OP[2]);
  not not_42 (not_42_out, OP[1]);
  not not_43 (not_43_out, OP[0]);
  or or_1 (or_1_out, and_1_out, and_2_out);
  and and_9 (out_3, not_38_out, not_39_out, not_40_out, not_41_out, not_42_out, not_43_out, or_1_out);
endmodule
